# Fritzing sketch Sketch (saved by Fritzing 0.9.2b)
breadboards: 2

parts:
  Part1 = Arduino Uno (Rev3)
  Disp1 = LBT2088AH [part_number=LBT2088AH]
  U1 = MAX7219 [package=dil24]
  R1 = Resistor [tolerance=±5% resistance=33k package="0402 [SMD]"]

nets:
  N1: Part1.D10_PWM/SS, U1.LOAD
  N2: Part1.D11_PWM/MOSI, U1.CLK
  N3: Part1.D12/MISO, U1.DIN
  5V: Part1.5V, U1.VCC, R1.Pin_1
  GND: Part1.GND, U1.GND, U1.GND2
  N4: Disp1.pin_9, U1.DIG7
  N5: Disp1.pin_10, U1.DIG6
  N6: Disp1.pin_11, U1.DIG5
  N7: Disp1.pin_12, U1.DIG4
  N8: Disp1.pin_13, U1.DIG3
  N9: Disp1.pin_14, U1.DIG2
  N10: Disp1.pin_15, U1.DIG1
  N11: Disp1.pin_16, U1.DIG0
  N12: U1.ISET, R1.Pin_0

notes:
  30000 ohm
