# Fritzing sketch Untitled Sketch 3 (saved by Fritzing 0.9.2b)
breadboards: 1

parts:
  Part1 = Arduino Uno (Rev3) - ICSP
  LED2 = smd LED [color="Yellow (585nm)" package="0805 [SMD]"]
  R1 = Resistor [tolerance=±5% resistance=220 package="0603 [SMD]"]
  R2 = Resistor [tolerance=±5% resistance=220 package="0603 [SMD]"]
  R3 = Resistor [tolerance=±5% resistance=220 package="0603 [SMD]"]
  LED6 = smd LED [color="Yellow (585nm)" package="0805 [SMD]"]
  LED7 = smd LED [color="Yellow (585nm)" package="0805 [SMD]"]
  LED8 = smd LED [color="Yellow (585nm)" package="0805 [SMD]"]
  LED9 = smd LED [color="Yellow (585nm)" package="0805 [SMD]"]
  LED10 = smd LED [color="Yellow (585nm)" package="0805 [SMD]"]
  R4 = Resistor [tolerance=±5% resistance=220 package="0603 [SMD]"]
  R5 = Resistor [tolerance=±5% resistance=220 package="0603 [SMD]"]
  R6 = Resistor [tolerance=±5% resistance=220 package="0603 [SMD]"]
  S1 = Momentary Switch [package=ksa_sealed_tac_switch]
  R7 = Resistor [tolerance=±5% resistance=220 package="0603 [SMD]"]
  LED11 = smd LED [color="Yellow (585nm)" package="0805 [SMD]"]
  R8 = Resistor [tolerance=±5% resistance=220 package="0603 [SMD]"]

nets:
  N1: Part1.ICSP_MISO, Part1.D12/MISO, LED6.anode
  N2: Part1.ICSP_MOSI, Part1.D11_PWM/MOSI, LED10.anode
  N3: Part1.D8, LED8.anode
  N4: Part1.D9_PWM, LED2.anode
  N5: Part1.D10_PWM/SS, LED7.anode
  N6: Part1.D13/SCK, LED9.anode
  N7: Part1.GND, R4.Pin_0, R5.Pin_0, R6.Pin_0, R7.Pin_0, R8.Pin_0
  N8: Part1.D4, S1.2, S1.4
  N9: LED2.cathode, R3.Pin_1
  N10: R1.Pin_0, R2.Pin_0, R3.Pin_0
  N11: R1.Pin_1, LED6.cathode
  N12: R2.Pin_1, LED7.cathode
  N13: LED8.cathode, R4.Pin_1
  N14: LED9.cathode, R5.Pin_1
  N15: LED10.cathode, R6.Pin_1
  N16: S1.1, S1.3
  N17: LED11.cathode, R8.Pin_1
